// Logisim project TN1.circ as structural Verilog: 1 circuit, main circuit main
module main (
  input  A,
  input  B,
  input  in_3,
  output A_prime,
  output AND,
  output OR,
  output NAND,
  output NOR,
  output XOR,
  output XNOR,
  output XOR3,
  output NAND3,
  output CHAIN
);

  wire nand_1_out;

  nand nand_1 (nand_1_out, A, B);
  not not_1 (A_prime, A);
  and and_1 (AND, A, B);
  or or_1 (OR, A, B);
  nand nand_2 (NAND, A, B);
  nor nor_1 (NOR, A, B);
  xor xor_1 (XOR, A, B);
  xnor xnor_1 (XNOR, A, B);
  xor xor_2 (XOR3, A, B, in_3);
  nand nand_3 (NAND3, A, B, in_3);
  nand nand_4 (CHAIN, nand_1_out, in_3);
endmodule
