// Logisim project TN3.circ as structural Verilog: 1 circuit, main circuit main
module main (
  input  A,
  input  B,
  input  C,
  input  D,
  output F
);

  wire A_prime_B_prime_CD_out, A_prime_B_prime_CD_prime_out, A_prime_BC_prime_D_out, A_prime_BCD_out,
       A_prime_out, AB_prime_CD_out, ABC_prime_D_out, B_prime_out, C_prime_out, D_prime_out;

  not A_prime (A_prime_out, A);
  not B_prime (B_prime_out, B);
  not C_prime (C_prime_out, C);
  not D_prime (D_prime_out, D);
  and A_prime_B_prime_CD_prime (A_prime_B_prime_CD_prime_out, A_prime_out, B_prime_out, C, D_prime_out);
  and A_prime_B_prime_CD (A_prime_B_prime_CD_out, A_prime_out, B_prime_out, C, D);
  and A_prime_BC_prime_D (A_prime_BC_prime_D_out, A_prime_out, B, C_prime_out, D);
  and A_prime_BCD (A_prime_BCD_out, A_prime_out, B, C, D);
  and AB_prime_CD (AB_prime_CD_out, A, B_prime_out, C, D);
  and ABC_prime_D (ABC_prime_D_out, A, B, C_prime_out, D);
  or or_1 (F, A_prime_B_prime_CD_prime_out, A_prime_B_prime_CD_out, A_prime_BC_prime_D_out, A_prime_BCD_out, AB_prime_CD_out, ABC_prime_D_out);
endmodule
