// Logisim project TN4_F_PoS.circ as structural Verilog: 1 circuit, main circuit main
module main (
  input  A,
  input  B,
  input  C,
  input  D,
  output out_5
);

  wire A_prime_B_prime_C_prime_out, A_prime_C_prime_D_out, A_prime_out, B_C_out, B_prime_D_out, B_prime_out,
       C_prime_out;

  not A_prime (A_prime_out, A);
  not B_prime (B_prime_out, B);
  not C_prime (C_prime_out, C);
  // NOT_Gate D_prime has open pins: in=D, out=open
  or B_C (B_C_out, B, C);
  or B_prime_D (B_prime_D_out, B_prime_out, D);
  or A_prime_B_prime_C_prime (A_prime_B_prime_C_prime_out, A_prime_out, B_prime_out, C_prime_out);
  or A_prime_C_prime_D (A_prime_C_prime_D_out, A_prime_out, C_prime_out, D);
  and and_1 (out_5, B_C_out, B_prime_D_out, A_prime_B_prime_C_prime_out, A_prime_C_prime_D_out);
endmodule
