// Logisim project TN4_F_SoP.circ as structural Verilog: 1 circuit, main circuit main
module main (
  input  A,
  input  B,
  input  C,
  input  D,
  output out_5
);

  wire A_prime_B_prime_C_out, A_prime_BD_out, A_prime_out, B_prime_CD_out, B_prime_out, BC_prime_D_out,
       C_prime_out;

  not A_prime (A_prime_out, A);
  not B_prime (B_prime_out, B);
  not C_prime (C_prime_out, C);
  // NOT_Gate D_prime has open pins: in=D, out=open
  and A_prime_B_prime_C (A_prime_B_prime_C_out, A_prime_out, B_prime_out, C);
  and B_prime_CD (B_prime_CD_out, B_prime_out, C, D);
  and BC_prime_D (BC_prime_D_out, B, C_prime_out, D);
  and A_prime_BD (A_prime_BD_out, A_prime_out, B, D);
  or or_1 (out_5, A_prime_B_prime_C_out, B_prime_CD_out, BC_prime_D_out, A_prime_BD_out);
endmodule
